// Logisim project mux-2.circ as structural Verilog: 1 circuit, main circuit main
module main (
  input  In0,
  input  In1,
  input  S,
  output Result
);

  wire and_1_out, and_2_out, not_1_out;

  not not_1 (not_1_out, S);
  and and_1 (and_1_out, In0, not_1_out);
  and and_2 (and_2_out, In1, S);
  or or_1 (Result, and_1_out, and_2_out);
endmodule
