// Logisim project Lab3Circuits.circ as structural Verilog
module alu_1bit_sub (
  input  BInvert,
  input  CarryIn,
  input  B,
  input  Op1,
  input  Op0,
  input  B_2,
  output Result,
  output CarryOut
);

  wire and_1_out, and_2_out, and_3_out, fa_1_1_sum, not_1_out, not_2_out, or_1_out, or_2_out;

  not not_1 (not_1_out, BInvert);
  not not_2 (not_2_out, B_2);
  and and_1 (and_1_out, not_1_out, B_2);
  and and_2 (and_2_out, BInvert, not_2_out);
  or or_1 (or_1_out, and_1_out, and_2_out);
  and and_3 (and_3_out, B, or_1_out);
  or or_2 (or_2_out, B, or_1_out);
  fa_1 fa_1_1 (.A(B), .B(or_1_out), .C(CarryIn), .Carry(CarryOut), .Sum(fa_1_1_sum));
  mux_4i mux_4i_1 (
    .In0(and_3_out), .In1(or_2_out), .In2(fa_1_1_sum), .Set1(Op1), .Set0(Op0), .Result(Result));  // open: In3
endmodule

module alu_1bit_slt (
  input  AInvert,
  input  BInvert,
  input  CarryIn,
  input  A,
  input  Op1,
  input  Op0,
  input  B,
  output Result,
  output Set,
  output Overflow,
  output CarryOut
);

  wire and_1_out, and_2_out, and_3_out, and_4_out, and_5_out, fa_1_1_sum, not_1_out, not_2_out, not_3_out,
       not_4_out, or_1_out, or_2_out, or_3_out;

  not not_1 (not_1_out, AInvert);
  not not_2 (not_2_out, A);
  and and_1 (and_1_out, not_1_out, A);
  and and_2 (and_2_out, AInvert, not_2_out);
  not not_3 (not_3_out, BInvert);
  and and_3 (and_3_out, not_3_out, B);
  and and_4 (and_4_out, BInvert, not_4_out);
  not not_4 (not_4_out, B);
  or or_1 (or_1_out, and_1_out, and_2_out);
  or or_2 (or_2_out, and_3_out, and_4_out);
  and and_5 (and_5_out, or_1_out, or_2_out);
  or or_3 (or_3_out, or_1_out, or_2_out);
  fa_1 fa_1_1 (.A(or_1_out), .B(or_2_out), .C(CarryIn), .Carry(CarryOut), .Sum(fa_1_1_sum));
  mux_4i mux_4i_1 (
    .In0(and_5_out), .In1(or_3_out), .In2(fa_1_1_sum), .Set1(Op1), .Set0(Op0), .Result(Result));  // open: In3
  xor xor_1 (Overflow, CarryIn, CarryOut);
  xor xor_2 (Set, CarryOut, Overflow);

  // Notes on the sheet:
  //   Operation
endmodule

module alu_6bit_mips (
  input  AInvert,
  input  BInvert,
  input  Operation,
  input  [5:0] A,
  input  [5:0] B,
  output Result0,
  output Result1,
  output Result2,
  output Equal,
  output Result3,
  output Result4,
  output Result5,
  output Overflow,
  output CarryOut
);

  wire alu_1bit_slt_1_p5, alu_1bit_slt_1_p9, alu_1bit_slt_1_p10, alu_1bit_slt_2_p9, alu_1bit_slt_2_p10,
       alu_1bit_slt_3_p5, alu_1bit_slt_3_p9, alu_1bit_slt_3_p10, alu_1bit_slt_4_p4, alu_1bit_slt_4_p8,
       alu_1bit_slt_4_p9, alu_1bit_slt_5_p6, alu_1bit_slt_5_p10, alu_1bit_slt_5_p11, alu_1bit_slt_6_p10;

  // alu_1bit_slt alu_1bit_slt_1: pin names not known; wires that end beside it: A[0], B[0], AInvert, BInvert, alu_1bit_slt_1_p5, Operation, Operation, Result0, alu_1bit_slt_1_p9, alu_1bit_slt_1_p10
  // alu_1bit_slt alu_1bit_slt_2: pin names not known; wires that end beside it: A[2], B[1], AInvert, alu_1bit_slt_1_p5, BInvert, Operation, Operation, Result1, alu_1bit_slt_2_p9, alu_1bit_slt_2_p10
  // alu_1bit_slt alu_1bit_slt_3: pin names not known; wires that end beside it: A[2], B[2], AInvert, BInvert, alu_1bit_slt_3_p5, Operation, Operation, Result2, alu_1bit_slt_3_p9, alu_1bit_slt_3_p10
  // alu_1bit_slt alu_1bit_slt_4: pin names not known; wires that end beside it: AInvert, BInvert, alu_1bit_slt_3_p5, alu_1bit_slt_4_p4, Operation, Operation, Result3, alu_1bit_slt_4_p8, alu_1bit_slt_4_p9
  // alu_1bit_slt alu_1bit_slt_5: pin names not known; wires that end beside it: A[4], B[4], AInvert, BInvert, alu_1bit_slt_4_p4, alu_1bit_slt_5_p6, Operation, Operation, Result4, alu_1bit_slt_5_p10, alu_1bit_slt_5_p11
  // alu_1bit_slt alu_1bit_slt_6: pin names not known; wires that end beside it: A[5], B[5], AInvert, BInvert, alu_1bit_slt_5_p6, CarryOut, Operation, Operation, Result5, alu_1bit_slt_6_p10, Overflow
  or or_1 (Equal, Result0, Result1, Result2, Result3, Result4, Result5);

  assign A[1] = A[2];
  assign B[3] = A[3];

  // Notes on the sheet:
  //   Need to put set bit back into input!
  //   Zero
endmodule
