// Logisim project Finale.circ as structural Verilog: 1 circuit, main circuit main2
module main2 (
);

  wire and_1_out, Clock_out, main_6_equal_zero, main_control_1_alusrc, main_control_1_branch,
       main_control_1_memtoreg, main_control_1_memwrite, main_control_1_regdst, main_control_1_regtowrite;
  wire [1:0] main_7_alucntl, main_7_alucntl_2, main_control_1_aluop;
  wire [4:0] multiplexer_1_out;
  wire [31:0] main_3_regdata1, main_3_regdata2, main_4_instruction_2, main_6_result, multiplexer_2_out,
       multiplexer_3_out, multiplexer_4_out, regular_32bit_adder_1_result, regular_32bit_adder_2_result,
       undriven, undriven_2, undriven_3, undriven_4;

  Clock Clock (.out(Clock_out));
  PC_main main_1 (.DataInput(multiplexer_4_out), .Clock(Clock_out), .DataOutput(undriven));
  Instruction_Memory_main main_2 (.ReadAddress(undriven), .Instruction(undriven_2));
  regular_32bit_adder regular_32bit_adder_1 (
    .B(32'h4), .A(undriven), .Result(regular_32bit_adder_1_result));  // open: Ainvert, Bnegate, CarryOut, Equal_Zero, Overflow
  Multiplexer #(.width(5), .enable("false")) multiplexer_1 (
    .in0(undriven_2[20:16]), .in1(undriven_2[15:11]), .out(multiplexer_1_out), .sel(main_control_1_regdst));
  main_control main_control_1 (
    .Instruction(undriven_2[31:26]), .RegDst(main_control_1_regdst), .RegtoWrite(main_control_1_regtowrite),
    .ALUSrc(main_control_1_alusrc), .MemtoReg(main_control_1_memtoreg), .MemWrite(main_control_1_memwrite),
    .Branch(main_control_1_branch), .ALUOp(main_control_1_aluop));
  Registers_main main_3 (
    .WriteData(multiplexer_3_out), .WriteReg(multiplexer_1_out[1:0]), .ReadReg2(undriven_2[17:16]),
    .ReadReg1(undriven_2[22:21]), .Clock(Clock_out), .Write(main_control_1_regtowrite),
    .RegData2(main_3_regdata2), .RegData1(main_3_regdata1));
  Sign_Extend_main main_4 (.Instruction(undriven_2[15:0]), .Instruction_2(main_4_instruction_2));
  Multiplexer #(.width(32), .enable("false")) multiplexer_2 (
    .in0(main_3_regdata2), .in1(main_4_instruction_2), .out(multiplexer_2_out), .sel(main_control_1_alusrc));
  Multiplexer #(.width(32), .enable("false")) multiplexer_3 (
    .in0(main_6_result), .in1(undriven_4), .out(multiplexer_3_out), .sel(main_control_1_memtoreg));
  Shift_left_main main_5 (.Instruction(main_4_instruction_2), .Instruction_2(undriven_3));
  ALU_main main_6 (
    .B(main_3_regdata1), .Ainvert(main_7_alucntl_2[1]), .Bnegate(main_7_alucntl_2[0]), .Oper(main_7_alucntl),
    .A(multiplexer_2_out), .Equal_Zero(main_6_equal_zero), .Result(main_6_result));  // open: CarryOut, Overflow
  ALU_Control_main main_7 (
    .Instruction(undriven_2[5:0]), .ALUOp(main_control_1_aluop), .ALUCntl({main_7_alucntl_2, main_7_alucntl}));
  regular_32bit_adder regular_32bit_adder_2 (
    .B(regular_32bit_adder_1_result), .A(undriven_3), .Result(regular_32bit_adder_2_result));  // open: Ainvert, Bnegate, CarryOut, Equal_Zero, Overflow
  and and_1 (and_1_out, main_control_1_branch, main_6_equal_zero);
  Data_Memory_main main_8 (
    .Address(main_6_result), .MemWrite(main_control_1_memwrite), .Clock(Clock_out), .ReadData(undriven_4));  // open: WriteData
  Multiplexer #(.width(32), .enable("false")) multiplexer_4 (
    .in0(regular_32bit_adder_1_result), .in1(regular_32bit_adder_2_result), .out(multiplexer_4_out),
    .sel(and_1_out));
endmodule
