// Logisim project Main-Control.circ as structural Verilog: 1 circuit, main circuit main-control
module main_control (
  input  [5:0] Instruction,
  output RegDst,
  output ALUSrc,
  output MemtoReg,
  output RegtoWrite,
  output MemWrite,
  output Branch,
  output [1:0] ALUOp
);

  wire not_1_out, not_2_out, not_3_out, not_4_out, not_5_out, not_6_out, not_7_out, not_8_out, not_9_out,
       not_10_out, not_11_out, not_12_out, not_13_out, not_14_out, not_15_out, not_16_out;

  not not_1 (not_1_out, Instruction[5]);
  not not_2 (not_2_out, Instruction[3]);
  not not_3 (not_3_out, Instruction[4]);
  not not_4 (not_4_out, Instruction[2]);
  not not_5 (not_5_out, Instruction[0]);
  not not_6 (not_6_out, Instruction[1]);
  and and_1 (ALUOp[1], not_1_out, not_3_out, not_2_out, not_4_out, not_6_out, not_5_out);
  not not_7 (not_7_out, Instruction[3]);
  not not_8 (not_8_out, Instruction[2]);
  not not_9 (not_9_out, Instruction[4]);
  and and_2 (MemtoReg, Instruction[5], not_9_out, not_7_out, not_8_out, Instruction[1], Instruction[0]);
  not not_10 (not_10_out, Instruction[4]);
  not not_11 (not_11_out, Instruction[2]);
  and and_3 (MemWrite, Instruction[5], not_10_out, Instruction[3], not_11_out, Instruction[1], Instruction[0]);
  not not_12 (not_12_out, Instruction[1]);
  not not_13 (not_13_out, Instruction[3]);
  not not_14 (not_14_out, Instruction[5]);
  not not_15 (not_15_out, Instruction[4]);
  not not_16 (not_16_out, Instruction[0]);
  and and_4 (ALUOp[0], not_14_out, not_15_out, not_13_out, Instruction[2], not_12_out, not_16_out);
  or or_1 (ALUSrc, MemtoReg, MemWrite);
  or or_2 (RegtoWrite, ALUOp[1], MemtoReg);

  assign Branch = ALUOp[0];
  assign RegDst = ALUOp[1];
endmodule
